// Logisim project TP1_exo1.circ as structural Verilog: 8 circuits, main circuit XOR
module XOR (
  input  x,
  input  y,
  output S
);

  wire and_1_out, and_2_out, not_1_out, not_2_out;

  not not_1 (not_1_out, y);
  not not_2 (not_2_out, x);
  and and_1 (and_1_out, not_1_out, x);
  and and_2 (and_2_out, y, not_2_out);
  or or_1 (S, and_1_out, and_2_out);

  // Notes on the sheet:
  //   XOR Circuit
endmodule

module _2_1_MUX (
  input  in_0,
  input  in_1,
  input  Select,
  output S
);

  wire and_1_out, and_2_out, not_1_out;

  not not_1 (not_1_out, Select);
  and and_1 (and_1_out, not_1_out, in_0);
  and and_2 (and_2_out, in_1, Select);
  or or_1 (S, and_1_out, and_2_out);

  // Notes on the sheet:
  //   2:1 MUX
endmodule

module _4_1_MUX (
  input  in_00,
  input  in_01,
  input  in_10,
  input  in_11,
  input  sel_0,
  input  sel_1,
  output out
);

  wire n2_1_mux_1_s, n2_1_mux_2_s;

  _2_1_MUX u_2_1_mux_1 (.in_0(in_00), .in_1(in_01), .S(n2_1_mux_1_s), .Select(sel_1));
  _2_1_MUX u_2_1_mux_2 (.in_0(in_10), .in_1(in_11), .S(n2_1_mux_2_s), .Select(sel_1));
  _2_1_MUX u_2_1_mux_3 (.in_0(n2_1_mux_1_s), .in_1(n2_1_mux_2_s), .S(out), .Select(sel_0));
endmodule

module x___0xFFFF__32bits (
  input  [31:0] IN,
  input  Select,
  output [31:0] OUT
);

  wire [31:0] bit_extender_1_out;

  assign OUT = IN & bit_extender_1_out;  // AND_Gate and_1, 32 bits wide
  assign bit_extender_1_out = {{31{Select}}, Select};  // Bit_Extender bit_extender_1
endmodule

module _4_1_MUX_32bits (
  input  [31:0] in_00,
  input  [31:0] in_01,
  input  [31:0] in_10,
  input  [31:0] in_11,
  input  [1:0] a,
  output [31:0] out
);

  wire [31:0] n2_1_mux_32bits_1_s, n2_1_mux_32bits_2_s;

  _2_1_MUX_32bits u_2_1_mux_32bits_1 (.in_0(in_00), .in_1(in_01), .S(n2_1_mux_32bits_1_s), .Select(a[0]));
  _2_1_MUX_32bits u_2_1_mux_32bits_2 (.in_0(in_10), .in_1(in_11), .S(n2_1_mux_32bits_2_s), .Select(a[0]));
  _2_1_MUX_32bits u_2_1_mux_32bits_3 (.in_0(n2_1_mux_32bits_1_s), .in_1(n2_1_mux_32bits_2_s), .S(out), .Select(a[1]));
endmodule

module _2_1_MUX_32bits (
  input  [31:0] in_0,
  input  [31:0] in_1,
  input  Select,
  output [31:0] S
);

  wire [31:0] and_1_out, and_2_out, bit_extender_1_out, not_1_out;

  assign bit_extender_1_out = {{31{Select}}, Select};  // Bit_Extender bit_extender_1
  assign not_1_out = ~bit_extender_1_out;  // NOT_Gate not_1, 32 bits wide
  assign and_1_out = not_1_out & in_0;  // AND_Gate and_1, 32 bits wide
  assign and_2_out = in_1 & bit_extender_1_out;  // AND_Gate and_2, 32 bits wide
  assign S = and_1_out | and_2_out;  // OR_Gate or_1, 32 bits wide

  // Notes on the sheet:
  //   2:1 MUX 32bits
  //   On utilise la propriété extend de type sign afin de remplacer le splitter
endmodule

module Encodeur (
  input  [7:0] In,
  output [2:0] S
);

  wire S0_out, S1_out, S2_out, Sec_out;

  or S0 (S0_out, In[1], In[3], In[5], In[7]);
  or S1 (S1_out, In[2], In[3], In[6], In[7]);
  or S2 (S2_out, In[4], In[5], In[6], In[7]);
  ExactlyOne Sec (
    .out(Sec_out), .in0(In[0]), .in1(In[1]), .in2(In[2]), .in3(In[3]), .in4(In[4]), .in5(In[5]), .in6(In[6]),
    .in7(In[7]));
  and S0_sec (S[0], Sec_out, S0_out);
  and S1_sec (S[1], Sec_out, S1_out);
  and S2_sec (S[2], Sec_out, S2_out);

  // Notes on the sheet:
  //   Encodeur BROSSARD Florian
  //   S0
  //   S1
  //   S2
endmodule

module UAL (
  input  [31:0] A,
  input  [31:0] B,
  input  [2:0] op,
  output [31:0] S
);

  wire [4:0] bit_extender_1_out;
  wire [31:0] adder_1_out, and_1_out, or_1_out, shifter_1_out, shifter_2_out, xor_1_out;

  Bit_Extender #(.in_width(32), .out_width(5)) bit_extender_1 (.in(A), .out(bit_extender_1_out));
  Adder #(.width(32)) adder_1 (.a(A), .b(B), .out(adder_1_out));  // open: cin, cout
  assign and_1_out = A & B;  // AND_Gate and_1, 32 bits wide
  assign or_1_out = A | B;  // OR_Gate or_1, 32 bits wide
  assign xor_1_out = A ^ B;  // XOR_Gate xor_1, 32 bits wide
  Shifter #(.width(32)) shifter_1 (.in(B), .\dist (bit_extender_1_out), .out(shifter_1_out));
  Shifter #(.width(32), .shift("lr")) shifter_2 (.in(B), .\dist (bit_extender_1_out), .out(shifter_2_out));
  Multiplexer #(.select(3), .width(32)) multiplexer_1 (
    .in0(adder_1_out), .in1(and_1_out), .in2(or_1_out), .in3(xor_1_out), .in4(shifter_1_out),
    .in5(shifter_2_out), .out(S), .sel(op), .en(1'b1));  // open: in6, in7

  // Notes on the sheet:
  //   UAL BROSSARD Florian
endmodule
