// Logisim project projet.circ as structural Verilog: 8 circuits, main circuit main
// aff
module main (
  input  in_1,
  input  in_2,
  output [8:0] cmd,
  output [2:0] out_4
);

  wire add, addi, aff, \and , and_1_out, and_8_out, andi, beq, bltz, bne, comparator_1_eq, control_nf_1__8,
       control_nf_1__20, control_nf_1__24, control_nf_1__25, control_nf_1__26, control_nf_1__27, etat_cv, H,
       jal, jr, keyboard_1_avail, lui, mem, neq, \nor , on, \or , or_2_out, or_3_out, or_4_out, or_5_out,
       ori, val_cv, \xor , xori;
  wire [4:0] multiplexer_2_out, num_rd, num_rs, num_rt, Shamt;
  wire [5:0] Co, Nf;
  wire [6:0] bit_extender_2_out, keyboard_1_data;
  wire [14:0] bit_extender_1_out;
  wire [31:0] ascii, car, cp, cp_4, lmm, lmm__2, lmm_ns, mips_ram_1_p7, mipsprogramrom_1_p1,
       multiplexer_1_out, multiplexer_3_out, multiplexer_4_out, multiplexer_5_out, multiplexer_6_out,
       res_mem, res_UAL, rs, rt;

  and and_1 (and_1_out, cmd[7], mem);
  decodage_adresse decodage_adresse_1 (.in_1(rt), .out_2(mem), .out_3(etat_cv), .out_4(val_cv), .out_5(aff));
  and and_2 (jr, control_nf_1__8, cmd[1]);
  controle_Co controle_co_1 (
    .in_1(Co), ._0(cmd[1]), .out_3(beq), ._5(bne), ._8(addi), .C(andi), .D(on), ._23(cmd[7]), .F(lui),
    ._2B(cmd[8]), ._12(andi), ._13(ori), ._14(xori), ._1_BLTZ(bltz), ._3(jal));
  Multiplexer #(.width(32), .enable("false")) multiplexer_1 (
    .in0(res_UAL), .in1(res_mem), .out(multiplexer_1_out), .sel(cmd[7]));
  Multiplexer #(.width(5), .enable("false")) multiplexer_2 (
    .in0(num_rd), .in1(num_rt), .out(multiplexer_2_out), .sel(cmd[1]));
  Bit_Extender #(.in_width(32), .out_width(15)) bit_extender_1 (.in(res_UAL), .out(bit_extender_1_out));
  control_Nf control_nf_1 (
    .in_1(Nf), ._20(control_nf_1__20), ._24(control_nf_1__24), ._25(control_nf_1__25),
    ._26(control_nf_1__26), ._27(control_nf_1__27), ._8(control_nf_1__8));
  // RegisterFile registerfile_1: pin names not known; wires that end beside it: multiplexer_1_out, H, cmd[6], multiplexer_2_out, num_rs, num_rt, in_1, rs, rt
  instruction_suivante Instruction_Suivante_CP (
    .cp(cp), .res_ual(res_UAL), .H(H), .R(in_1), .mx6(cmd[5]), .neq(neq), .cp_4(cp_4));
  // MIPS_RAM mips_ram_1: pin names not known; wires that end beside it: bit_extender_1_out, rt, and_1_out, cmd[8], H, in_1, mips_ram_1_p7, cp
  and and_3 (add, control_nf_1__20, cmd[1]);
  and and_4 (\nor , cmd[1], control_nf_1__27);
  or or_1 (cmd[5], bne, beq);
  Multiplexer #(.width(32), .enable("false")) multiplexer_3 (
    .in0(rs), .in1(cp_4), .out(multiplexer_3_out), .sel(cmd[5]));
  Multiplexer #(.width(32), .enable("false")) multiplexer_4 (
    .in0(lmm), .in1(lmm__2), .out(multiplexer_4_out), .sel(cmd[5]));
  Multiplexer #(.width(32), .enable("false")) multiplexer_5 (
    .in0(mips_ram_1_p7), .in1(ascii), .out(multiplexer_5_out), .sel(val_cv));
  and and_5 (\and , control_nf_1__24, cmd[1]);
  nor nor_1 (cmd[6], cmd[5], cmd[8]);
  UAL ual_1 (.rs(multiplexer_3_out), .rt(multiplexer_6_out), .in_3(out_4), .out_4(res_UAL));
  Multiplexer #(.width(32), .enable("false")) multiplexer_6 (
    .in0(multiplexer_4_out), .in1(rt), .out(multiplexer_6_out), .sel(cmd[1]));
  Multiplexer #(.width(32), .enable("false")) multiplexer_7 (
    .in0(multiplexer_5_out), .in1(car), .out(res_mem), .sel(etat_cv));
  and and_6 (\or , cmd[1], control_nf_1__25);
  and and_7 (\xor , cmd[1], control_nf_1__26);
  or or_2 (or_2_out, \xor , xori);
  or or_3 (or_3_out, \or , ori);
  or or_4 (or_4_out, \and , andi);
  Comparator #(.width(32)) comparator_1 (.a(rs), .b(rt), .eq(comparator_1_eq));  // open: gt, lt
  // MIPSProgramROM mipsprogramrom_1: pin names not known; wires that end beside it: mipsprogramrom_1_p1
  decodeur decodeur_1 (
    .in_1(mipsprogramrom_1_p1), .lmm_ns(lmm_ns), .lmm__2(lmm__2), .lmm(lmm), .Nf(Nf), .Shamt(Shamt),
    .num_rd(num_rd), .num_rt(num_rt), .num_rs(num_rs), .Co(Co));
  or or_5 (or_5_out, bne, beq);
  Clock clock_1 (.out(H));
  Operation operation_1 (
    .\xor (or_2_out), .Ou(or_3_out), .decalage(in_2), .Et(or_4_out), .jal(jr), .out_7(out_4), .autre(or_5_out));
  not not_1 (neq, comparator_1_eq);
  and and_8 (and_8_out, H, val_cv);
  Keyboard keyboard_1 (.clk(and_8_out), .re(1'b1), .clr(in_1), .avail(keyboard_1_avail), .data(keyboard_1_data));
  Bit_Extender #(.in_width(32), .out_width(7)) bit_extender_2 (.in(rt), .out(bit_extender_2_out));
  TTY tty_1 (.data(bit_extender_2_out), .clk(H), .we(aff), .clr(in_1));
  assign car = {{31{1'b0}}, keyboard_1_avail};  // Bit_Extender bit_extender_3
  assign ascii = {{25{1'b0}}, keyboard_1_data};  // Bit_Extender bit_extender_4

  assign {cmd[4:2], cmd[0]} = {{2{cmd[5]}}, cmd[7], cmd[1]};

  // Other names for the same wires on the sheet: _3R = cmd[1]; mx1 = cmd[1]; mx2 = cmd[1]; mx4 = cmd[5]; mx5 = cmd[5];
  //   mx6 = cmd[5]; er = cmd[6]; em = cmd[7]; ln = cmd[7]; lw = cmd[7]; mx3 = cmd[7]; lm = cmd[8]; sw = cmd[8];
  //   Op[2:0] = out_4; R = in_1
endmodule

module controle_Co (
  input  [5:0] in_1,
  output _0,
  output out_3,
  output _5,
  output _8,
  output C,
  output D,
  output _23,
  output F,
  output _2B,
  output _12,
  output _13,
  output _14,
  output _1_BLTZ,
  output _3
);

  wire not_1_out, not_2_out, not_3_out, not_4_out, not_5_out, not_6_out, not_7_out, not_8_out, not_9_out,
       not_10_out, not_11_out, not_12_out, not_13_out, not_14_out, not_15_out, not_16_out, not_17_out,
       not_18_out, not_19_out, not_20_out, not_21_out, not_22_out, not_23_out, not_24_out, not_25_out,
       not_26_out, not_27_out, not_28_out, not_29_out, not_30_out, not_31_out, not_32_out, not_33_out,
       not_34_out, not_35_out, not_36_out, not_37_out, not_38_out, not_39_out, not_40_out, not_41_out,
       not_42_out, not_43_out, not_44_out, not_45_out, not_46_out, not_47_out, not_48_out, not_49_out,
       not_50_out, not_51_out, not_52_out, not_53_out, not_54_out;

  not not_1 (not_1_out, in_1[2]);
  and and_1 (_2B, in_1[0], in_1[1], not_1_out, in_1[3], not_2_out, in_1[5]);
  not not_2 (not_2_out, in_1[4]);
  not not_3 (not_3_out, in_1[2]);
  not not_4 (not_4_out, in_1[3]);
  and and_2 (_23, in_1[0], in_1[1], not_3_out, not_4_out, not_5_out, in_1[5]);
  not not_5 (not_5_out, in_1[4]);
  not not_6 (not_6_out, in_1[1]);
  not not_7 (not_7_out, in_1[3]);
  not not_8 (not_8_out, in_1[4]);
  not not_9 (not_9_out, in_1[5]);
  not not_10 (not_10_out, in_1[0]);
  not not_11 (not_11_out, in_1[1]);
  and and_3 (_8, not_10_out, in_1[3], not_11_out, not_12_out, not_13_out, not_14_out);
  not not_12 (not_12_out, in_1[2]);
  not not_13 (not_13_out, in_1[4]);
  not not_14 (not_14_out, in_1[5]);
  not not_15 (not_15_out, in_1[0]);
  not not_16 (not_16_out, in_1[1]);
  and and_4 (C, not_15_out, not_16_out, in_1[2], in_1[3], not_17_out, not_18_out);
  not not_17 (not_17_out, in_1[4]);
  not not_18 (not_18_out, in_1[5]);
  not not_19 (not_19_out, in_1[1]);
  not not_20 (not_20_out, in_1[4]);
  not not_21 (not_21_out, in_1[5]);
  not not_22 (not_22_out, in_1[4]);
  not not_23 (not_23_out, in_1[5]);
  not not_24 (not_24_out, in_1[0]);
  not not_25 (not_25_out, in_1[2]);
  not not_26 (not_26_out, in_1[3]);
  not not_27 (not_27_out, in_1[5]);
  not not_28 (not_28_out, in_1[2]);
  not not_29 (not_29_out, in_1[3]);
  not not_30 (not_30_out, in_1[5]);
  not not_31 (not_31_out, in_1[0]);
  not not_32 (not_32_out, in_1[1]);
  not not_33 (not_33_out, in_1[3]);
  not not_34 (not_34_out, in_1[5]);
  not not_35 (not_35_out, in_1[1]);
  not not_36 (not_36_out, in_1[2]);
  not not_37 (not_37_out, in_1[3]);
  not not_38 (not_38_out, in_1[4]);
  not not_39 (not_39_out, in_1[5]);
  not not_40 (not_40_out, in_1[0]);
  not not_41 (not_41_out, in_1[2]);
  not not_42 (not_42_out, in_1[3]);
  not not_43 (not_43_out, in_1[4]);
  not not_44 (not_44_out, in_1[5]);
  not not_45 (not_45_out, in_1[0]);
  not not_46 (not_46_out, in_1[1]);
  and and_5 (_5, in_1[0], not_6_out, in_1[2], not_7_out, not_8_out, not_9_out);
  and and_6 (D, in_1[0], not_19_out, in_1[2], in_1[3], not_20_out, not_21_out);
  and and_7 (F, in_1[0], in_1[1], in_1[2], in_1[3], not_22_out, not_23_out);
  and and_8 (_12, not_24_out, in_1[1], not_25_out, not_26_out, in_1[4], not_27_out);
  and and_9 (_13, in_1[0], in_1[1], not_28_out, not_29_out, in_1[4], not_30_out);
  and and_10 (_14, not_31_out, not_32_out, in_1[2], not_33_out, in_1[4], not_34_out);
  and and_11 (_1_BLTZ, in_1[0], not_35_out, not_36_out, not_37_out, not_38_out, not_39_out);
  and and_12 (_3, not_40_out, in_1[1], not_41_out, not_42_out, not_43_out, not_44_out);
  not not_47 (not_47_out, in_1[0]);
  not not_48 (not_48_out, in_1[1]);
  not not_49 (not_49_out, in_1[2]);
  and and_13 (_0, not_47_out, not_48_out, not_49_out, not_50_out, not_51_out, not_52_out);
  not not_50 (not_50_out, in_1[3]);
  not not_51 (not_51_out, in_1[4]);
  not not_52 (not_52_out, in_1[5]);
  and and_14 (out_3, not_45_out, not_46_out, in_1[2], not_53_out, not_54_out, not_52_out);
  not not_53 (not_53_out, in_1[3]);
  not not_54 (not_54_out, in_1[4]);
endmodule

module control_Nf (
  input  [5:0] in_1,
  output _20,
  output _24,
  output _25,
  output _26,
  output _27,
  output _8
);

  wire not_1_out, not_2_out, not_3_out, not_4_out, not_5_out, not_6_out, not_7_out, not_8_out, not_9_out,
       not_10_out, not_11_out, not_12_out, not_13_out, not_14_out, not_15_out, not_16_out, not_17_out,
       not_18_out, not_19_out, not_20_out, not_21_out, not_22_out;

  not not_1 (not_1_out, in_1[0]);
  not not_2 (not_2_out, in_1[1]);
  not not_3 (not_3_out, in_1[2]);
  and and_1 (_20, not_1_out, not_2_out, not_3_out, not_4_out, not_5_out, in_1[5]);
  not not_4 (not_4_out, in_1[3]);
  not not_5 (not_5_out, in_1[4]);
  not not_6 (not_6_out, in_1[0]);
  not not_7 (not_7_out, in_1[1]);
  and and_2 (_24, not_6_out, not_7_out, in_1[2], not_8_out, not_9_out, in_1[5]);
  not not_8 (not_8_out, in_1[3]);
  not not_9 (not_9_out, in_1[4]);
  not not_10 (not_10_out, in_1[3]);
  not not_11 (not_11_out, in_1[1]);
  and and_3 (_25, in_1[0], not_10_out, not_11_out, in_1[2], not_12_out, in_1[5]);
  not not_12 (not_12_out, in_1[4]);
  not not_13 (not_13_out, in_1[0]);
  and and_4 (_26, not_13_out, in_1[1], in_1[2], not_14_out, not_15_out, in_1[5]);
  not not_14 (not_14_out, in_1[3]);
  not not_15 (not_15_out, in_1[4]);
  not not_16 (not_16_out, in_1[3]);
  not not_17 (not_17_out, in_1[4]);
  not not_18 (not_18_out, in_1[0]);
  not not_19 (not_19_out, in_1[1]);
  not not_20 (not_20_out, in_1[2]);
  not not_21 (not_21_out, in_1[4]);
  not not_22 (not_22_out, in_1[5]);
  and and_5 (_27, in_1[0], in_1[1], in_1[2], not_16_out, not_17_out, in_1[5]);
  and and_6 (_8, not_18_out, not_19_out, not_20_out, in_1[3], not_21_out, not_22_out);
endmodule

module decodeur (
  input  [31:0] in_1,
  output [31:0] lmm_ns,
  output [31:0] lmm__2,
  output [31:0] lmm,
  output [5:0] Nf,
  output [4:0] Shamt,
  output [4:0] num_rd,
  output [4:0] num_rt,
  output [4:0] num_rs,
  output [5:0] Co
);

  assign lmm_ns = {{16{1'b0}}, in_1[15:0]};  // Bit_Extender bit_extender_1
  assign lmm = {{16{in_1[15]}}, in_1[15:0]};  // Bit_Extender bit_extender_2
  Shifter #(.width(32)) shifter_1 (.in(lmm_ns), .\dist (5'b00010), .out(lmm__2));

  assign Co = in_1[31:26];
  assign Nf = in_1[5:0];
  assign num_rd = in_1[15:11];
  assign num_rs = in_1[25:21];
  assign num_rt = in_1[20:16];
  assign Shamt = in_1[10:6];
endmodule

module UAL (
  input  [31:0] rs,
  input  [31:0] rt,
  input  [2:0] in_3,
  output [31:0] out_4
);

  wire [31:0] adder_1_out, and_1_out, or_1_out, shifter_1_out, xor_1_out;

  Adder #(.width(32)) adder_1 (.a(rs), .b(rt), .out(adder_1_out));  // open: cin, cout
  assign and_1_out = rs & rt;  // AND_Gate and_1, 32 bits wide
  assign or_1_out = rs | rt;  // OR_Gate or_1, 32 bits wide
  assign xor_1_out = rs ^ rt;  // XOR_Gate xor_1, 32 bits wide
  Shifter #(.width(32)) shifter_1 (.in(rt), .\dist (5'b10000), .out(shifter_1_out));
  Multiplexer #(.select(3), .width(32), .enable("false")) multiplexer_1 (
    .in0(adder_1_out), .in1(and_1_out), .in2(or_1_out), .in3(xor_1_out), .in4(shifter_1_out), .in5(rs),
    .in6(rs), .out(out_4), .sel(in_3));  // open: in7
endmodule

module Operation (
  input  \xor ,
  input  Ou,
  input  decalage,
  input  Et,
  input  jal,
  input  autre,
  output [2:0] out_7
);

  or or_1 (out_7[1], \xor , autre, Et);
  or or_2 (out_7[0], \xor , jal, Ou);
  or or_3 (out_7[2], decalage, autre, jal);
endmodule

module instruction_suivante (
  input  H,
  input  R,
  input  mx6,
  input  neq,
  input  [31:0] res_ual,
  output [31:0] cp,
  output [31:0] cp_4
);

  wire and_1_out;
  wire [31:0] multiplexer_1_out;

  Multiplexer #(.width(32), .enable("false")) multiplexer_1 (
    .in0(cp_4), .in1(res_ual), .out(multiplexer_1_out), .sel(and_1_out));
  and and_1 (and_1_out, mx6, neq);
  Register #(.width(32)) register_1 (.D(multiplexer_1_out), .en(1'b1), .Q(cp), .clk(H), .clr(R));
  Adder #(.width(32)) adder_1 (.a(32'h4), .b(cp), .out(cp_4));  // open: cin, cout
endmodule

module decodage_adresse (
  input  [31:0] in_1,
  output out_2,
  output out_3,
  output out_4,
  output out_5
);

  wire comparator_1_gt, comparator_2_lt;

  Comparator #(.width(32)) comparator_1 (.a(32'h3fff), .b(in_1), .gt(comparator_1_gt));  // open: eq, lt
  Comparator #(.width(32)) comparator_2 (.a(32'h2000), .b(in_1), .lt(comparator_2_lt));  // open: gt, eq
  Comparator #(.width(32)) comparator_3 (.a(in_1), .b(32'h7f00), .eq(out_3));  // open: gt, lt
  Comparator #(.width(32)) comparator_4 (.a(in_1), .b(32'h7f04), .eq(out_4));  // open: gt, lt
  Comparator #(.width(32)) comparator_5 (.a(in_1), .b(32'h7f0c), .eq(out_5));  // open: gt, lt
  and and_1 (out_2, comparator_1_gt, comparator_2_lt);
endmodule
