// Logisim project projet_FB.circ as structural Verilog: 11 circuits, main circuit Calcul
module Calcul (
  input  H,
  input  er,
  input  R,
  input  mx1,
  input  mx2,
  input  mx3,
  input  mx4,
  input  mx5,
  input  [2:0] op,
  input  [4:0] num_rd,
  input  [4:0] num_rt,
  input  [4:0] num_rs,
  input  [31:0] res_mem,
  input  [31:0] cp_4,
  input  [31:0] Imm,
  input  [31:0] Imm__2,
  output [31:0] rs,
  output [31:0] res_ual,
  output [31:0] rt
);

  wire [4:0] multiplexer_2_out;
  wire [31:0] multiplexer_1_out, multiplexer_3_out, multiplexer_4_out, multiplexer_5_out;

  Multiplexer #(.width(32), .enable("false")) multiplexer_1 (
    .in0(res_ual), .in1(res_mem), .out(multiplexer_1_out), .sel(mx3));
  Multiplexer #(.width(5), .enable("false")) multiplexer_2 (
    .in0(num_rt), .in1(num_rd), .out(multiplexer_2_out), .sel(mx1));
  // RegisterFile registerfile_1: pin names not known; wires that end beside it: multiplexer_1_out, H, er, multiplexer_2_out, num_rs, num_rt, R, rs, rt
  Multiplexer #(.width(32), .enable("false")) multiplexer_3 (
    .in0(Imm), .in1(Imm__2), .out(multiplexer_3_out), .sel(mx5));
  Multiplexer #(.width(32), .enable("false")) multiplexer_4 (.in0(rs), .in1(cp_4), .out(multiplexer_4_out), .sel(mx4));
  UAL ual_1 (.rs(multiplexer_4_out), .rt_Imm16(multiplexer_5_out), .Op(op), .res(res_ual));
  Multiplexer #(.width(32), .enable("false")) multiplexer_5 (
    .in0(multiplexer_3_out), .in1(rt), .out(multiplexer_5_out), .sel(mx2));
endmodule

module UAL (
  input  [31:0] rs,
  input  [31:0] rt_Imm16,
  input  [2:0] Op,
  output [31:0] res
);

  wire adder_1_cout;
  wire [31:0] adder_1_out, and_1_out, or_1_out, subtractor_1_out, xor_1_out;

  Adder #(.width(32)) adder_1 (.a(rs), .b(rt_Imm16), .out(adder_1_out), .cout(adder_1_cout));  // open: cin
  Subtractor #(.width(32)) subtractor_1 (
    .a(rs), .b(rt_Imm16), .out(subtractor_1_out), .bin(adder_1_cout));  // open: bout
  assign and_1_out = rs & rt_Imm16;  // AND_Gate and_1, 32 bits wide
  assign or_1_out = rs | rt_Imm16;  // OR_Gate or_1, 32 bits wide
  assign xor_1_out = rs ^ rt_Imm16;  // XOR_Gate xor_1, 32 bits wide
  Multiplexer #(.select(3), .width(32), .enable("false")) multiplexer_1 (
    .in0(adder_1_out), .in1(subtractor_1_out), .in2(and_1_out), .in3(or_1_out), .in5(xor_1_out), .out(res),
    .sel(Op));  // open: in4, in6, in7
endmodule

module \Memoire_Donnée  (
  input  em,
  input  mem,
  input  [31:0] res
);

  wire and_1_out, H, lm, R;
  wire [15:0] bit_extender_1_out;
  wire [31:0] res_mem, rt;

  and and_1 (and_1_out, em, mem);
  Bit_Extender #(.in_width(32), .\type ("sign")) bit_extender_1 (.in(res), .out(bit_extender_1_out));
  // MIPS_RAM mips_ram_1: pin names not known; wires that end beside it: bit_extender_1_out, rt, and_1_out, lm, H, R, res_mem

  // Other names for the same wires on the sheet: res_ual[31:0] = res
endmodule

module Instruction_Suivante (
  input  [31:0] res_ual,
  input  R,
  input  H,
  input  neq,
  input  mx6,
  output [31:0] cp_4,
  output [31:0] cp
);

  wire and_1_out;
  wire [31:0] multiplexer_1_out;

  Adder #(.width(32)) adder_1 (.a(32'h4), .b(cp), .out(cp_4));  // open: cin, cout
  Multiplexer #(.width(32), .enable("false")) multiplexer_1 (
    .in0(cp_4), .in1(res_ual), .out(multiplexer_1_out), .sel(and_1_out));
  and and_1 (and_1_out, neq, mx6);
  Register #(.width(32)) register_1 (.D(multiplexer_1_out), .en(1'b1), .Q(cp), .clk(H), .clr(R));
endmodule

module main (
  input  R
);

  wire aff, and_1_out, comparator_1_eq, etat_cv, H, keyboard_1_avail, mem, neq, val_cv;
  wire [2:0] op;
  wire [4:0] num_rd, num_rs, num_rt, Shamt;
  wire [5:0] Co, Nf;
  wire [6:0] bit_extender_1_out, keyboard_1_data;
  wire [8:0] cmd;
  wire [31:0] ascii, car, cp, cp_4, Imm, Imm__2, Imm_ns, mipsprogramrom_1_p2, res_mem, res_ual, rs, rs_ual,
       rt;

  decodage_adresse decodage_adresse_1 (.rt(rt), .mem(mem), .etat_cv(etat_cv), .val_cv(val_cv), .aff(aff));
  Comparator #(.width(32)) comparator_1 (.a(rs), .b(rt), .eq(comparator_1_eq));  // open: gt, lt
  Instruction_Suivante instruction_suivante_1 (
    .H(H), .R(R), .cp_4(cp_4), .cp(cp), .res_ual(rs_ual), .neq(neq), .mx6(cmd[5]));
  not not_1 (neq, comparator_1_eq);
  // MIPSProgramROM mipsprogramrom_1: pin names not known; wires that end beside it: cp, mipsprogramrom_1_p2
  Decode decode_1 (
    .Op(mipsprogramrom_1_p2), .Imm_ns(Imm_ns), .Imm__2(Imm__2), .Imm(Imm), .Nf(Nf), .Shamt(Shamt),
    .num_rd(num_rd), .num_rt(num_rs), .num_rs(num_rt), .Co(Co));
  Keyboard keyboard_1 (.clk(and_1_out), .re(1'b1), .clr(R), .avail(keyboard_1_avail), .data(keyboard_1_data));
  and and_1 (and_1_out, H, val_cv);
  Calcul calcul_1 (
    .H(H), .er(cmd[6]), .R(R), .mx1(cmd[0]), .mx2(cmd[1]), .mx3(cmd[2]), .mx4(cmd[3]), .mx5(cmd[4]), .op(op),
    .num_rd(num_rd), .num_rt(num_rt), .num_rs(num_rs), .res_mem(res_mem), .cp_4(cp_4), .Imm(Imm),
    .Imm__2(Imm__2), .rt(rt), .rs(rs), .res_ual(res_ual));
  Clock Clk (.out(H));
  Bit_Extender #(.in_width(32), .out_width(7)) bit_extender_1 (.in(rt), .out(bit_extender_1_out));
  assign ascii = {{25{1'b0}}, keyboard_1_data};  // Bit_Extender bit_extender_2
  assign car = {{31{1'b0}}, keyboard_1_avail};  // Bit_Extender bit_extender_3
  TTY tty_1 (.data(bit_extender_1_out), .clk(H), .we(aff), .clr(R));
  CMD u_CMD (.Co(Co), .Nf(Nf), .Op(op), .cmd(cmd));

  // Other names for the same wires on the sheet: mx1 = cmd[0]; mx2 = cmd[1]; mx3 = cmd[2]; mx4 = cmd[3]; mx5 = cmd[4];
  //   mx6 = cmd[5]; er = cmd[6]; em = cmd[7]; lm = cmd[8]
endmodule

module Decode (
  input  [31:0] Op,
  output [31:0] Imm_ns,
  output [31:0] Imm__2,
  output [31:0] Imm,
  output [5:0] Nf,
  output [4:0] Shamt,
  output [4:0] num_rd,
  output [4:0] num_rt,
  output [4:0] num_rs,
  output [5:0] Co
);

  assign Imm_ns = {{16{1'b0}}, Op[15:0]};  // Bit_Extender bit_extender_1
  assign Imm = {{16{Op[15]}}, Op[15:0]};  // Bit_Extender bit_extender_2
  Shifter #(.width(32)) shifter_1 (.in(Imm_ns), .\dist (5'b00010), .out(Imm__2));

  assign Co = Op[31:26];
  assign Nf = Op[5:0];
  assign num_rd = Op[15:11];
  assign num_rs = Op[25:21];
  assign num_rt = Op[20:16];
  assign Shamt = Op[10:6];
endmodule

module decodage_adresse (
  input  [31:0] rt,
  output mem,
  output etat_cv,
  output val_cv,
  output aff
);

  wire comparator_1_gt, comparator_2_lt;

  Comparator #(.width(32)) comparator_1 (.a(32'h3fff), .b(rt), .gt(comparator_1_gt));  // open: eq, lt
  Comparator #(.width(32)) comparator_2 (.a(32'h2000), .b(rt), .lt(comparator_2_lt));  // open: gt, eq
  Comparator #(.width(32)) comparator_3 (.a(rt), .b(32'h7f00), .eq(etat_cv));  // open: gt, lt
  Comparator #(.width(32)) comparator_4 (.a(rt), .b(32'h7f04), .eq(val_cv));  // open: gt, lt
  Comparator #(.width(32)) comparator_5 (.a(rt), .b(32'h7f0c), .eq(aff));  // open: gt, lt
  and and_1 (mem, comparator_1_gt, comparator_2_lt);
endmodule

module CMD (
  input  [5:0] Co,
  input  [5:0] Nf,
  output [2:0] Op,
  output [8:0] cmd
);

  wire add, addi, \and , andi, beq, bltz, bne, jal, jr, lui, Nf_8, Nf_20, Nf_22, Nf_24, Nf_25, Nf_26, Nf_27,
       \nor , \or , or_3_out, ori, sub, \xor , xori;

  Controle_Nf controle_nf_1 (
    .in_1(Nf), ._20(Nf_20), ._24(Nf_24), ._25(Nf_25), ._26(Nf_26), ._27(Nf_27), ._22(Nf_22), ._8(Nf_8));
  and and_1 (add, cmd[1], Nf_20);
  and and_2 (\and , cmd[1], Nf_24);
  and and_3 (\or , cmd[1], Nf_25);
  and and_4 (\xor , cmd[1], Nf_26);
  and and_5 (\nor , cmd[1], Nf_27);
  and and_6 (jr, cmd[1], Nf_8);
  and and_7 (sub, cmd[1], Nf_22);
  Controle_Co u_Co (
    .in_1(Co), ._0(cmd[1]), ._4(beq), ._5(bne), ._8(addi), .C(andi), .D(ori), ._23(cmd[7]), .F(lui),
    ._2B(cmd[8]), ._14(xori), ._1_BLTZ(bltz), ._3(jal));  // open: _12, _13
  // OR_Gate or_1 has open pins: in0=\or , in1=ori, out=open
  // OR_Gate or_2 has open pins: in0=\and , in1=andi, out=open
  or or_3 (or_3_out, \xor , xori);
  or or_4 (cmd[5], bne, beq);
  nor nor_1 (cmd[6], cmd[5], cmd[8]);
  Op op_1 (.Op(Op));  // open: or_ori, decalage, and_andi, sub, xor_xori

  assign {cmd[4:2], cmd[0]} = {{2{cmd[5]}}, cmd[7], cmd[1]};

  // Other names for the same wires on the sheet: _3R = cmd[1]; lw = cmd[7]; sw = cmd[8]
endmodule

module Controle_Co (
  input  [5:0] in_1,
  output _0,
  output _4,
  output _5,
  output _8,
  output C,
  output D,
  output _23,
  output F,
  output _2B,
  output _12,
  output _13,
  output _14,
  output _1_BLTZ,
  output _3
);

  wire not_1_out, not_2_out, not_3_out, not_4_out, not_5_out, not_6_out, not_7_out, not_8_out, not_9_out,
       not_10_out, not_11_out, not_12_out, not_13_out, not_14_out, not_15_out, not_16_out, not_17_out,
       not_18_out, not_19_out, not_20_out, not_21_out, not_22_out, not_23_out, not_24_out, not_25_out,
       not_26_out, not_27_out, not_28_out, not_29_out, not_30_out, not_31_out, not_32_out, not_33_out,
       not_34_out, not_35_out, not_36_out, not_37_out, not_38_out, not_39_out, not_40_out, not_41_out,
       not_42_out, not_43_out, not_44_out, not_45_out, not_46_out, not_47_out, not_48_out, not_49_out,
       not_50_out, not_51_out, not_52_out, not_53_out, not_54_out;

  not not_1 (not_1_out, in_1[2]);
  and and_1 (_2B, in_1[0], in_1[1], not_1_out, in_1[3], not_2_out, in_1[5]);
  not not_2 (not_2_out, in_1[4]);
  not not_3 (not_3_out, in_1[2]);
  and and_2 (_23, in_1[0], in_1[1], not_3_out, not_4_out, not_5_out, in_1[5]);
  not not_4 (not_4_out, in_1[3]);
  not not_5 (not_5_out, in_1[4]);
  not not_6 (not_6_out, in_1[1]);
  not not_7 (not_7_out, in_1[3]);
  not not_8 (not_8_out, in_1[4]);
  not not_9 (not_9_out, in_1[5]);
  not not_10 (not_10_out, in_1[0]);
  not not_11 (not_11_out, in_1[1]);
  and and_3 (_8, not_10_out, in_1[3], not_11_out, not_12_out, not_13_out, not_14_out);
  not not_12 (not_12_out, in_1[2]);
  not not_13 (not_13_out, in_1[4]);
  not not_14 (not_14_out, in_1[5]);
  not not_15 (not_15_out, in_1[0]);
  not not_16 (not_16_out, in_1[1]);
  and and_4 (C, not_15_out, not_16_out, in_1[2], in_1[3], not_17_out, not_18_out);
  not not_17 (not_17_out, in_1[4]);
  not not_18 (not_18_out, in_1[5]);
  not not_19 (not_19_out, in_1[1]);
  not not_20 (not_20_out, in_1[4]);
  not not_21 (not_21_out, in_1[5]);
  not not_22 (not_22_out, in_1[4]);
  not not_23 (not_23_out, in_1[5]);
  not not_24 (not_24_out, in_1[0]);
  not not_25 (not_25_out, in_1[2]);
  not not_26 (not_26_out, in_1[3]);
  not not_27 (not_27_out, in_1[5]);
  not not_28 (not_28_out, in_1[2]);
  not not_29 (not_29_out, in_1[3]);
  not not_30 (not_30_out, in_1[5]);
  not not_31 (not_31_out, in_1[0]);
  not not_32 (not_32_out, in_1[1]);
  not not_33 (not_33_out, in_1[3]);
  not not_34 (not_34_out, in_1[5]);
  not not_35 (not_35_out, in_1[1]);
  not not_36 (not_36_out, in_1[2]);
  not not_37 (not_37_out, in_1[3]);
  not not_38 (not_38_out, in_1[4]);
  not not_39 (not_39_out, in_1[5]);
  not not_40 (not_40_out, in_1[0]);
  not not_41 (not_41_out, in_1[2]);
  not not_42 (not_42_out, in_1[3]);
  not not_43 (not_43_out, in_1[4]);
  not not_44 (not_44_out, in_1[5]);
  not not_45 (not_45_out, in_1[0]);
  not not_46 (not_46_out, in_1[1]);
  and and_5 (_5, in_1[0], not_6_out, in_1[2], not_7_out, not_8_out, not_9_out);
  and and_6 (D, in_1[0], not_19_out, in_1[2], in_1[3], not_20_out, not_21_out);
  and and_7 (F, in_1[0], in_1[1], in_1[2], in_1[3], not_22_out, not_23_out);
  and and_8 (_12, not_24_out, in_1[1], not_25_out, not_26_out, in_1[4], not_27_out);
  and and_9 (_13, in_1[0], in_1[1], not_28_out, not_29_out, in_1[4], not_30_out);
  and and_10 (_14, not_31_out, not_32_out, in_1[2], not_33_out, in_1[4], not_34_out);
  and and_11 (_1_BLTZ, in_1[0], not_35_out, not_36_out, not_37_out, not_38_out, not_39_out);
  and and_12 (_3, not_40_out, in_1[1], not_41_out, not_42_out, not_43_out, not_44_out);
  not not_47 (not_47_out, in_1[0]);
  not not_48 (not_48_out, in_1[1]);
  not not_49 (not_49_out, in_1[2]);
  and and_13 (_0, not_47_out, not_48_out, not_49_out, not_50_out, not_51_out, not_52_out);
  not not_50 (not_50_out, in_1[3]);
  not not_51 (not_51_out, in_1[4]);
  not not_52 (not_52_out, in_1[5]);
  and and_14 (_4, not_45_out, not_46_out, in_1[2], not_53_out, not_54_out, not_52_out);
  not not_53 (not_53_out, in_1[3]);
  not not_54 (not_54_out, in_1[4]);
endmodule

module Controle_Nf (
  input  [5:0] in_1,
  output _20,
  output _24,
  output _25,
  output _26,
  output _27,
  output _22,
  output _8
);

  wire not_1_out, not_2_out, not_3_out, not_4_out, not_5_out, not_6_out, not_7_out, not_8_out, not_9_out,
       not_10_out, not_11_out, not_12_out, not_13_out, not_14_out, not_15_out, not_16_out, not_17_out,
       not_18_out, not_19_out, not_20_out, not_21_out, not_22_out;

  and and_1 (_22, ~in_1[0], in_1[1], ~in_1[2], ~in_1[3], ~in_1[4], in_1[5]);  // AND_Gate
  not not_1 (not_1_out, in_1[0]);
  not not_2 (not_2_out, in_1[1]);
  not not_3 (not_3_out, in_1[2]);
  and and_2 (_20, not_1_out, not_2_out, not_3_out, not_4_out, not_5_out, in_1[5]);
  not not_4 (not_4_out, in_1[3]);
  not not_5 (not_5_out, in_1[4]);
  not not_6 (not_6_out, in_1[0]);
  not not_7 (not_7_out, in_1[1]);
  and and_3 (_24, not_6_out, not_7_out, in_1[2], not_8_out, not_9_out, in_1[5]);
  not not_8 (not_8_out, in_1[3]);
  not not_9 (not_9_out, in_1[4]);
  not not_10 (not_10_out, in_1[3]);
  not not_11 (not_11_out, in_1[1]);
  and and_4 (_25, in_1[0], not_10_out, not_11_out, in_1[2], not_12_out, in_1[5]);
  not not_12 (not_12_out, in_1[4]);
  not not_13 (not_13_out, in_1[0]);
  and and_5 (_26, not_13_out, in_1[1], in_1[2], not_14_out, not_15_out, in_1[5]);
  not not_14 (not_14_out, in_1[3]);
  not not_15 (not_15_out, in_1[4]);
  not not_16 (not_16_out, in_1[3]);
  not not_17 (not_17_out, in_1[4]);
  not not_18 (not_18_out, in_1[0]);
  not not_19 (not_19_out, in_1[1]);
  not not_20 (not_20_out, in_1[2]);
  not not_21 (not_21_out, in_1[4]);
  not not_22 (not_22_out, in_1[5]);
  and and_6 (_27, in_1[0], in_1[1], in_1[2], not_16_out, not_17_out, in_1[5]);
  and and_7 (_8, not_18_out, not_19_out, not_20_out, in_1[3], not_21_out, not_22_out);
endmodule

module Op (
  input  or_ori,
  input  decalage,
  input  and_andi,
  input  sub,
  input  xor_xori,
  output [2:0] Op
);

  or or_1 (Op[0], sub, or_ori, xor_xori);
  or or_2 (Op[1], and_andi, or_ori);
  buf or_3 (Op[2], xor_xori);  // OR_Gate

  // Other names for the same wires on the sheet: and = and_andi; or = or_ori; xor = xor_xori
endmodule
