// Logisim project tests.circ as structural Verilog: 1 circuit, main circuit main
module main (
  input  [5:0] Commande,
  output [5:0] Sortie_6bits
);

  wire [5:0] multiplexer_1_out, multiplexer_2_out;

  Multiplexer #(.select(5), .width(6)) multiplexer_1 (
    .out(multiplexer_1_out), .sel(Commande[4:0]));  // open: in0, in1, in2, in3, in4, in5, in6, in7, in8, in9, in10, in11, in12, in13, in14, in15, in16, in17, in18, in19, in20, in21, in22, in23, in24, in25, in26, in27, in28, in29, in30, in31, en
  Multiplexer #(.select(5), .width(6)) multiplexer_2 (
    .out(multiplexer_2_out), .sel(Commande[4:0]));  // open: in0, in1, in2, in3, in4, in5, in6, in7, in8, in9, in10, in11, in12, in13, in14, in15, in16, in17, in18, in19, in20, in21, in22, in23, in24, in25, in26, in27, in28, in29, in30, in31, en
  Multiplexer #(.width(6)) multiplexer_3 (
    .in0(multiplexer_1_out), .in1(multiplexer_2_out), .out(Sortie_6bits), .sel(Commande[5]));  // open: en
endmodule
